# Fritzing sketch Untitled Sketch (saved by Fritzing 0.9.10b)
breadboards: 1

parts:
  R1 = PHOTOCELL [package=photocell-kit]
  R2 = Resistor [tolerance=±5% power=0.25 resistance=10k package=THT]
  DHT1 = DHT11 Humitidy and Temperature Sensor
  Компонент1 = Arduino Uno (Rev3)
  R3 = Resistor [tolerance=±5% power=0.25 resistance=10k package=THT]

nets:
  VDD: R1.P$1, R2.Pin_1, DHT1.VDD, Компонент1.5V
  N1: R1.P$2, Компонент1.A0, R3.Pin_0
  N2: R2.Pin_0, DHT1.DATA, Компонент1.D2
  GND: DHT1.GND, Компонент1.GND, R3.Pin_1

custom parts:
  DHT11 Humitidy and Temperature Sensor: DHT11 Humidity and Temperature Sensor

// code stored in the sketch: Untitled.ino
<?xml version="1.0" encoding="UTF-8"?>
<document version="0.9.3b" partnumber="my_project" source="Fritzing">
  <title>Arduino DHT11 + LDR</title>
  <parts>
    <!-- Arduino Uno -->
    <part ref="1" partnumber="arduino-uno" name="Arduino Uno" url="https://fritzing.org/parts/arduino-uno/">
      <location>
        <x>100</x>
        <y>100</y>
      </location>
    </part>

    <!-- DHT11 -->
    <part ref="2" partnumber="dht11" name="DHT11" url="https://fritzing.org/parts/dht11/">
      <location>
        <x>300</x>
        <y>150</y>
      </location>
    </part>

    <!-- ???????????? -->
    <part ref="3" partnumber="photoresistor" name="????????????" url="https://fritzing.org/parts/photoresistor/">
      <location>
        <x>300</x>
        <y>250</y>
      </location>
    </part>

    <!-- ???????? 10 ??? -->
    <part ref="4" partnumber="resistor" name="???????? 10 ???" url="https://fritzing.org/parts/resistor/">
      <location>
        <x>350</x>
        <y>250</y>
      </location>
    </part>
  </parts>

  <connections>
    <!-- DHT11 ??????????? -->
    <connection from="1:5V" to="2:1" />
    <connection from="1:GND" to="2:4" />
    <connection from="1:2" to="2:2" />
    <connection from="2:2" to="2:1" resistance="10k" /> <!-- ????????????? ???????? -->

    <!-- ???????????? + ???????? -->
    <connection from="1:5V" to="3:1" />
    <connection from="3:2" to="4:1" />
    <connection from="4:2" to="1:GND" />
    <connection from="3:2" to="1:A0" /> <!-- ?????????? ???? -->
  </connections>

  <views>
    <breadboardView>
      <layer ref="breadboard" />
    </breadboardView>
  </views>
</document>
